# Fritzing sketch Arduino_ESP (saved by Fritzing 0.9.3b)

parts:
  Part1 = Arduino Mega ADK (Rev3)
  U1 = ESP8266 WiFi Module [part_number=ESP8266]

nets:
  N1: Part1.D19/RX1, U1.TXD
  N2: Part1.D18/TX1, U1.RXD
  N3: Part1.RESET, U1.RST
  3V3: Part1.3V3, U1.VCC, U1.CH_PD
  GND: Part1.GND, U1.GND

custom parts:
  ESP8266 WiFi Module: Generic WiFi Module based on the ESP8266 with onboard PCB antenna and UART communications
